# Fritzing sketch 1 channel (saved by Fritzing 0.9.4)
circuit board: 4.98584cm x 6.8934cm

parts:
  ESP1 = ESP 12E
  +1 = screw terminal, 2 pins
  R1 = Resistor [tolerance=±5% resistance=220 package=THT]
  R2 = Resistor [tolerance=±5% resistance=220 package=THT]
  R3 = Resistor [tolerance=±5% resistance=220 package=THT]
  R4 = Resistor [tolerance=±5% resistance=220 package=THT]
  R5 = Resistor [tolerance=±5% resistance=220 package=THT]
  +2 = screw terminal, 2 pins
  Power_conversion1 = HLK-PM01
  Fuse2 = Fuse with Handler [part_number=Htc-15m]
  U2 = Voltage Regulator [package=to220-adj]
  U3 = Voltage Regulator [package=to220-adj]
  U4 = 555 Timer [package="DIP8 [THT]"]
  R6 = Resistor [tolerance=±5% resistance=220 package=THT]
  R7 = Resistor [tolerance=±5% resistance=220 package=THT]
  R8 = Resistor [tolerance=±5% resistance=220 package=THT]
  R9 = Resistor [tolerance=±5% resistance=220 package=THT]
  +3 = screw terminal, 2 pins
  +4 = screw terminal, 2 pins

nets:
  N1: ESP1.GPIO0, R3.Pin_1
  N2: ESP1.GPIO2, R2.Pin_0
  N3: ESP1.GPIO15, R1.Pin_1
  N4: ESP1.GND, +1.pin2, R1.Pin_0, Power_conversion1.-Vo, U2.IN, U4.Trigger, +4.pin2
  N5: ESP1.VCC, +1.pin1, R2.Pin_1, R3.Pin_0, R4.Pin_0, R5.Pin_1, U2.OUT, R8.Pin_0
  N6: ESP1.GPIO14, R8.Pin_1, +4.pin1
  N7: ESP1.GPIO16, R6.Pin_0
  N8: ESP1.EN, R5.Pin_0
  N9: ESP1.RST, R4.Pin_1
  N10: +2.pin1, Power_conversion1.AC#1, +3.pin1
  N11: +2.pin2, Power_conversion1.AC#0, U3.IN, R9.Pin_0
  N12: Power_conversion1.+Vo, Fuse2.Connector2
  N13: Fuse2.Connector1, U2.ADJ
  N14: U3.ADJ, U4.Threshold, R9.Pin_1
  N15: U3.OUT, R7.Pin_0, +3.pin2
  N16: U4.Ground, R6.Pin_1
  N17: U4.Vcc_Supply_Voltage, R7.Pin_1

custom parts:
  ESP 12E: ESP 12e module with spi interface and wifi connection
