# Fritzing sketch 3 channel (saved by Fritzing 0.9.4)
circuit board: 7.26036cm x 6.2271cm
breadboards: 1

parts:
  ESP1 = ESP 12E
  +1 = screw terminal, 2 pins
  R1 = Resistor [tolerance=±5% resistance=220 package=THT]
  R2 = Resistor [tolerance=±5% resistance=220 package=THT]
  R3 = Resistor [tolerance=±5% resistance=220 package=THT]
  R4 = Resistor [tolerance=±5% resistance=220 package=THT]
  R5 = Resistor [tolerance=±5% resistance=220 package=THT]
  +2 = screw terminal, 2 pins
  Power_conversion1 = HLK-PM01
  Fuse2 = Fuse with Handler [part_number=Htc-15m]
  U2 = Voltage Regulator [package=to220-adj]
  U3 = Voltage Regulator [package=to220-adj]
  U4 = 555 Timer [package="DIP8 [THT]"]
  R6 = Resistor [tolerance=±5% resistance=220 package=THT]
  R7 = Resistor [tolerance=±5% resistance=220 package=THT]
  R8 = Resistor [tolerance=±5% resistance=220 package=THT]
  R9 = Resistor [tolerance=±5% resistance=220 package=THT]
  R10 = Resistor [tolerance=±5% resistance=220 package=THT]
  R12 = Resistor [tolerance=±5% resistance=220 package=THT]
  R13 = Resistor [tolerance=±5% resistance=220 package=THT]
  R14 = Resistor [tolerance=±5% resistance=220 package=THT]
  R15 = Resistor [tolerance=±5% resistance=220 package=THT]
  R16 = Resistor [tolerance=±5% resistance=220 package=THT]
  R17 = Resistor [tolerance=±5% resistance=220 package=THT]
  R18 = Resistor [tolerance=±5% resistance=220 package=THT]
  U5 = 555 Timer [package="DIP8 [THT]"]
  U6 = 555 Timer [package="DIP8 [THT]"]
  U7 = Voltage Regulator [package=to220-adj]
  U8 = Voltage Regulator [package=to220-adj]

nets:
  N1: ESP1.GPIO5, R17.Pin_1
  N2: ESP1.GPIO4, R18.Pin_0
  N3: ESP1.GPIO0, R3.Pin_1
  N4: ESP1.GPIO2, R2.Pin_0
  N5: ESP1.GPIO15, R1.Pin_1
  N6: ESP1.GND, +1.pin2, R1.Pin_0, Power_conversion1.-Vo, U2.IN
  N7: ESP1.VCC, +1.pin1, R2.Pin_1, R3.Pin_0, R4.Pin_0, R5.Pin_1, U2.OUT, R6.Pin_1, R7.Pin_1
  N8: ESP1.GPIO13, R7.Pin_0
  N9: ESP1.GPIO12, R8.Pin_0
  N10: ESP1.GPIO14, R6.Pin_0
  N11: ESP1.EN, R5.Pin_0
  N12: ESP1.ADC, R9.Pin_1
  N13: ESP1.RST, R4.Pin_1
  N14: +2.pin1, Power_conversion1.AC#1
  N15: +2.pin2, Power_conversion1.AC#0
  N16: Power_conversion1.+Vo, Fuse2.Connector2
  N17: Fuse2.Connector1, U2.ADJ
  N18: U3.ADJ, U4.Threshold, R12.Pin_0
  N19: U3.IN, R12.Pin_1
  N20: U3.OUT, R16.Pin_0
  N21: U4.Ground, R18.Pin_1
  N22: U4.Vcc_Supply_Voltage, R16.Pin_1
  N23: R9.Pin_0, U5.Ground
  N24: R10.Pin_0, U5.Threshold, U8.ADJ
  N25: R10.Pin_1, U8.IN
  N26: R13.Pin_0, U5.Vcc_Supply_Voltage
  N27: R13.Pin_1, U8.OUT
  N28: R14.Pin_0, U7.OUT
  N29: R14.Pin_1, U6.Vcc_Supply_Voltage
  N30: R15.Pin_0, U7.IN
  N31: R15.Pin_1, U6.Threshold, U7.ADJ
  N32: R17.Pin_0, U6.Ground

custom parts:
  ESP 12E: ESP 12e module with spi interface and wifi connection
