# Fritzing sketch Programmer esp-12 (saved by Fritzing 0.9.4)
circuit board: 4.87866cm x 5.19729cm
breadboards: 1

parts:
  ESP1 = ESP 12E
  + = screw terminal, 2 pins
  R1 = Resistor [tolerance=±5% resistance=220 package=THT]
  R2 = Resistor [tolerance=±5% resistance=220 package=THT]
  R3 = Resistor [tolerance=±5% resistance=220 package=THT]
  R4 = Resistor [tolerance=±5% resistance=220 package=THT]
  R5 = Resistor [tolerance=±5% resistance=220 package=THT]
  S2 = Momentary Switch [package=ksa_sealed_tac_switch]
  S3 = Momentary Switch [package=ksa_sealed_tac_switch]
  LED1 = LEDs [package=led10mm]
  LED2 = LEDs [package=led10mm]
  R6 = Resistor [tolerance=±5% resistance=220 package=THT]
  R7 = Resistor [tolerance=±5% resistance=220 package=THT]
  JP1 = Header 6 [package=1x06-smd]
  C1 = Ceramic Capacitor [capacitance=100nF package="100 mil [THT, multilayer]"]

nets:
  N1: ESP1.GPIO0, R3.Pin_1, S2.1, LED2.C
  N2: ESP1.GPIO2, R2.Pin_1
  N3: ESP1.GPIO15, R1.Pin_0
  N4: ESP1.GND, +.pin2, R1.Pin_1
  N5: ESP1.MOSI, ESP1.GPIO10
  N6: ESP1.VCC, +.pin1, R2.Pin_0, R3.Pin_0, R4.Pin_1, R5.Pin_1, R6.Pin_1, R7.Pin_1, JP1.3
  N7: ESP1.EN, R4.Pin_0
  N8: ESP1.RST, R5.Pin_0, S3.3, LED1.A, C1.0
  N9: S2.4, S3.2
  N10: LED1.C, R7.Pin_0
  N11: LED2.A, R6.Pin_0
  N12: JP1.6, C1.1

custom parts:
  ESP 12E: ESP 12e module with spi interface and wifi connection
