# Fritzing sketch jig esp12 (saved by Fritzing 0.9.4)
circuit board: 2.68534cm x 3.23007cm
breadboards: 1

parts:
  ESP1 = ESP 12E
  +1 = screw terminal, 2 pins
  R1 = Resistor [tolerance=±5% resistance=220 package=THT]
  R2 = Resistor [tolerance=±5% resistance=220 package=THT]
  R3 = Resistor [tolerance=±5% resistance=220 package=THT]
  R4 = Resistor [tolerance=±5% resistance=220 package=THT]
  R5 = Resistor [tolerance=±5% resistance=220 package=THT]
  JP2 = Header 6 [package=molex-1x6-ra_lock]
  JP3 = Header 6 [package=molex-1x6-ra_lock]

nets:
  N1: ESP1.TX0, JP2.1
  N2: ESP1.RX0, JP2.2
  N3: ESP1.GPIO5, JP2.3
  N4: ESP1.GPIO4, JP2.4
  N5: ESP1.GPIO0, R3.Pin_1
  N6: ESP1.GPIO2, R2.Pin_0
  N7: ESP1.GPIO15, R1.Pin_1
  N8: ESP1.GND, +1.pin2, R1.Pin_0
  N9: ESP1.VCC, +1.pin1, R2.Pin_1, R3.Pin_0, R4.Pin_0, R5.Pin_1
  N10: ESP1.GPIO13, JP3.2
  N11: ESP1.GPIO12, JP3.3
  N12: ESP1.GPIO14, JP3.4
  N13: ESP1.GPIO16, JP3.5
  N14: ESP1.EN, R5.Pin_0
  N15: ESP1.RST, R4.Pin_1

custom parts:
  ESP 12E: ESP 12e module with spi interface and wifi connection
